# Fritzing sketch PIR (saved by Fritzing 0.8.3b)
breadboards: 1

parts:
  Raspberry_Pi_rev1 = Raspberry Pi rev2
  LED1 = LED - 5mm [color="Blue (430nm)" package="5 mm [THT]"]
  R2 = Resistor [tolerance=±5% resistance=330 package=THT]
  PIR1 = PIR sensor

nets:
  3V3: Raspberry_Pi_rev1.3V3, PIR1.VDD
  GND: Raspberry_Pi_rev1.GND, LED1.cathode, PIR1.GND
  N1: Raspberry_Pi_rev1.GPIO_22, LED1.anode, R2.Pin_0
  N2: R2.Pin_1, PIR1.SIG
